// Logisim project main.circ as structural Verilog: 14 circuits, main circuit TwoBitAdder
module TwoBitAdder (
  input  [1:0] A,
  input  [1:0] B,
  input  C_in,
  output [1:0] Sum,
  output C_out
);

  wire and_1_out, and_2_out, and_3_out, and_4_out, or_1_out, xor_1_out, xor_3_out;

  xor xor_1 (xor_1_out, A[0], B[0]);
  xor xor_2 (Sum[0], xor_1_out, C_in);
  and and_1 (and_1_out, xor_1_out, C_in);
  and and_2 (and_2_out, A[0], B[0]);
  or or_1 (or_1_out, and_1_out, and_2_out);
  xor xor_3 (xor_3_out, A[1], B[1]);
  xor xor_4 (Sum[1], xor_3_out, or_1_out);
  and and_3 (and_3_out, xor_3_out, or_1_out);
  and and_4 (and_4_out, A[1], B[1]);
  or or_2 (C_out, and_3_out, and_4_out);

  // Notes on the sheet:
  //   External Carry
  //   S1
  //   Two Bit Adder
  //   B1
  //   B2
  //   S2
  //   Carry-out
endmodule

module FourBitAdder (
  input  [3:0] A,
  input  [3:0] B,
  input  C_in,
  output [3:0] Sum,
  output C_out
);

  wire twobitadder_1_c_out;

  TwoBitAdder twobitadder_1 (.A(A[1:0]), .B(B[1:0]), .C_in(C_in), .Sum(Sum[1:0]), .C_out(twobitadder_1_c_out));
  TwoBitAdder twobitadder_2 (.A(A[3:2]), .B(B[3:2]), .C_in(twobitadder_1_c_out), .Sum(Sum[3:2]), .C_out(C_out));
endmodule

module EightBitAdder (
  input  [7:0] A,
  input  [7:0] B,
  input  C_in,
  output [7:0] Sum,
  output C_out
);

  wire fourbitadder_1_c_out;

  FourBitAdder fourbitadder_1 (.A(A[3:0]), .B(B[3:0]), .C_in(C_in), .Sum(Sum[3:0]), .C_out(fourbitadder_1_c_out));
  FourBitAdder fourbitadder_2 (.A(A[7:4]), .B(B[7:4]), .C_in(fourbitadder_1_c_out), .Sum(Sum[7:4]), .C_out(C_out));
endmodule

module SixteenBitAdder (
  input  [15:0] A,
  input  [15:0] B,
  input  C_in,
  output [15:0] Sum,
  output C_out
);

  wire eightbitadder_1_c_out;

  EightBitAdder eightbitadder_1 (.A(A[7:0]), .B(B[7:0]), .C_in(C_in), .Sum(Sum[7:0]), .C_out(eightbitadder_1_c_out));
  EightBitAdder eightbitadder_2 (
    .A(A[15:8]), .B(B[15:8]), .C_in(eightbitadder_1_c_out), .Sum(Sum[15:8]), .C_out(C_out));
endmodule

module SixteenBitSubtractor (
  input  [15:0] A,
  input  [15:0] B,
  output [15:0] out_3,
  output borrow_out
);

  wire [15:0] not_1_out;

  assign not_1_out = ~B;  // NOT_Gate not_1, 16 bits wide
  SixteenBitAdder sixteenbitadder_1 (.A(A), .B(not_1_out), .C_in(1'b1), .Sum(out_3), .C_out(borrow_out));
endmodule

module SixteenBitIncrement (
  input  [15:0] A,
  output [15:0] Increment
);

  SixteenBitAdder sixteenbitadder_1 (.A(A), .B({16{1'b0}}), .C_in(1'b1), .Sum(Increment));  // open: C_out
endmodule

module SixteenBitDecrement (
  input  [15:0] A,
  output [15:0] Decrement
);

  SixteenBitSubtractor sixteenbitsubtractor_1 (.A(A), .B(16'h1), .out_3(Decrement));  // open: borrow_out
endmodule

module Enabled_D_FlipFlop (
  input  D,
  input  clk,
  input  Enable,
  output Q,
  output Q_not
);

  wire multiplexer_1_out;

  Multiplexer multiplexer_1 (.in0(Q), .in1(D), .out(multiplexer_1_out), .sel(Enable));
  D_Flip_Flop d_ff_1 (.D(multiplexer_1_out), .clk(clk), .Q(Q), .Qn(Q_not));  // open: preset, reset
endmodule

module MyRegister (
  input  [7:0] input_bits,
  input  clk,
  input  enable,
  output [7:0] output_bits
);

  Enabled_D_FlipFlop enabled_d_flipflop_1 (
    .D(input_bits[0]), .clk(clk), .Enable(enable), .Q(output_bits[0]));  // open: Q_not
  Enabled_D_FlipFlop enabled_d_flipflop_2 (
    .D(input_bits[1]), .clk(clk), .Enable(enable), .Q(output_bits[1]));  // open: Q_not
  Enabled_D_FlipFlop enabled_d_flipflop_3 (
    .D(input_bits[2]), .clk(clk), .Enable(enable), .Q(output_bits[2]));  // open: Q_not
  Enabled_D_FlipFlop enabled_d_flipflop_4 (
    .D(input_bits[3]), .clk(clk), .Enable(enable), .Q(output_bits[3]));  // open: Q_not
  Enabled_D_FlipFlop enabled_d_flipflop_5 (
    .D(input_bits[4]), .clk(clk), .Enable(enable), .Q(output_bits[4]));  // open: Q_not
  Enabled_D_FlipFlop enabled_d_flipflop_6 (
    .D(input_bits[5]), .clk(clk), .Enable(enable), .Q(output_bits[5]));  // open: Q_not
  Enabled_D_FlipFlop enabled_d_flipflop_7 (
    .D(input_bits[6]), .clk(clk), .Enable(enable), .Q(output_bits[6]));  // open: Q_not
  Enabled_D_FlipFlop enabled_d_flipflop_8 (
    .D(input_bits[7]), .clk(clk), .Enable(enable), .Q(output_bits[7]));  // open: Q_not
endmodule

module Sixteen_Bit_Register (
  input  [15:0] input_bits,
  input  clk,
  input  enable,
  output [15:0] out_4
);

  MyRegister myregister_1 (.input_bits(input_bits[7:0]), .clk(clk), .enable(enable), .output_bits(out_4[7:0]));
  MyRegister myregister_2 (.input_bits(input_bits[15:8]), .clk(clk), .enable(enable), .output_bits(out_4[15:8]));
endmodule

module Twelve_Bit_Register (
  input  [11:0] input_bits,
  input  clk,
  input  LD,
  output [11:0] output_bits
);

  Enabled_D_FlipFlop enabled_d_flipflop_1 (
    .D(input_bits[0]), .clk(clk), .Enable(LD), .Q(output_bits[0]));  // open: Q_not
  Enabled_D_FlipFlop enabled_d_flipflop_2 (
    .D(input_bits[1]), .clk(clk), .Enable(LD), .Q(output_bits[1]));  // open: Q_not
  Enabled_D_FlipFlop enabled_d_flipflop_3 (
    .D(input_bits[2]), .clk(clk), .Enable(LD), .Q(output_bits[2]));  // open: Q_not
  Enabled_D_FlipFlop enabled_d_flipflop_4 (
    .D(input_bits[3]), .clk(clk), .Enable(LD), .Q(output_bits[3]));  // open: Q_not
  Enabled_D_FlipFlop enabled_d_flipflop_5 (
    .D(input_bits[4]), .clk(clk), .Enable(LD), .Q(output_bits[4]));  // open: Q_not
  Enabled_D_FlipFlop enabled_d_flipflop_6 (
    .D(input_bits[5]), .clk(clk), .Enable(LD), .Q(output_bits[5]));  // open: Q_not
  Enabled_D_FlipFlop enabled_d_flipflop_7 (
    .D(input_bits[6]), .clk(clk), .Enable(LD), .Q(output_bits[6]));  // open: Q_not
  Enabled_D_FlipFlop enabled_d_flipflop_8 (
    .D(input_bits[7]), .clk(clk), .Enable(LD), .Q(output_bits[7]));  // open: Q_not
  Enabled_D_FlipFlop enabled_d_flipflop_9 (
    .D(input_bits[8]), .clk(clk), .Enable(LD), .Q(output_bits[8]));  // open: Q_not
  Enabled_D_FlipFlop enabled_d_flipflop_10 (
    .D(input_bits[9]), .clk(clk), .Enable(LD), .Q(output_bits[9]));  // open: Q_not
  Enabled_D_FlipFlop enabled_d_flipflop_11 (
    .D(input_bits[10]), .clk(clk), .Enable(LD), .Q(output_bits[10]));  // open: Q_not
  Enabled_D_FlipFlop enabled_d_flipflop_12 (
    .D(input_bits[11]), .clk(clk), .Enable(LD), .Q(output_bits[11]));  // open: Q_not
endmodule

module TwoxFour_Decoder (
  input  [1:0] select_bits,
  input  enable,
  output [3:0] out_3
);

  wire not_1_out, not_2_out;

  not not_1 (not_1_out, select_bits[0]);
  not not_2 (not_2_out, select_bits[1]);
  and and_1 (out_3[0], not_2_out, not_1_out, enable);
  and and_2 (out_3[1], select_bits[0], not_2_out, enable);
  and and_3 (out_3[2], select_bits[1], not_1_out, enable);
  and and_4 (out_3[3], select_bits[1], select_bits[0], enable);
endmodule

module ThreebyEight_Decoder (
  input  [2:0] select_bits,
  input  enable,
  output [7:0] output_bits
);

  wire and_1_out, and_2_out, not_1_out;

  not not_1 (not_1_out, select_bits[2]);
  and and_1 (and_1_out, not_1_out, enable);
  and and_2 (and_2_out, select_bits[2], enable);
  TwoxFour_Decoder twoxfour_decoder_1 (.select_bits(select_bits[1:0]), .enable(and_1_out), .out_3(output_bits[3:0]));
  TwoxFour_Decoder twoxfour_decoder_2 (.select_bits(select_bits[1:0]), .enable(and_2_out), .out_3(output_bits[7:4]));
endmodule

module FourbySixteen_Decoder (
  input  [3:0] in_1,
  input  enable,
  output [15:0] out_3
);

  wire and_1_out, and_2_out, not_1_out;

  not not_1 (not_1_out, in_1[3]);
  and and_1 (and_1_out, in_1[3], enable);
  and and_2 (and_2_out, not_1_out, enable);
  ThreebyEight_Decoder threebyeight_decoder_1 (.select_bits(in_1[2:0]), .enable(and_2_out), .output_bits(out_3[7:0]));
  ThreebyEight_Decoder threebyeight_decoder_2 (.select_bits(in_1[2:0]), .enable(and_1_out), .output_bits(out_3[15:8]));
endmodule
